// Logisim project ALU.circ as structural Verilog: 8 circuits, main circuit full_adder_2bits
module main (
);

  mux2 mux2_1 ();  // open: A, B, in_3, out_4
endmodule

module mux2 (
  input  A,
  input  B,
  input  in_3,
  output out_4
);

  wire and_1_out, and_2_out, not_1_out;

  not not_1 (not_1_out, in_3);
  and and_1 (and_1_out, A, not_1_out);
  and and_2 (and_2_out, B, in_3);
  or or_1 (out_4, and_1_out, and_2_out);
endmodule

module mux4 (
  input  in_1,
  input  in_2,
  input  in_3,
  input  in_4,
  input  in_5,
  input  in_6,
  output out_7
);

  wire mux2_1_out_4, mux2_2_out_4;

  mux2 mux2_1 (.A(in_1), .B(in_2), .in_3(in_5), .out_4(mux2_1_out_4));
  mux2 mux2_2 (.A(in_3), .B(in_4), .in_3(in_5), .out_4(mux2_2_out_4));
  mux2 mux2_3 (.A(mux2_1_out_4), .B(mux2_2_out_4), .in_3(in_6), .out_4(out_7));
endmodule

module mux8 (
  input  in_1,
  input  in_2,
  input  in_3,
  input  in_4,
  input  in_5,
  input  in_6,
  input  in_7,
  input  in_8,
  input  in_9,
  input  in_10,
  input  in_11,
  output out_12
);

  wire mux4_1_out_7, mux4_2_out_7;

  mux4 mux4_1 (.in_1(in_1), .in_2(in_2), .in_3(in_3), .in_4(in_4), .in_5(in_9), .in_6(in_10), .out_7(mux4_1_out_7));
  mux4 mux4_2 (.in_1(in_5), .in_2(in_6), .in_3(in_7), .in_4(in_8), .in_5(in_9), .in_6(in_10), .out_7(mux4_2_out_7));
  mux2 mux2_1 (.A(mux4_1_out_7), .B(mux4_2_out_7), .in_3(in_11), .out_4(out_12));
endmodule

module mux_64_a_8 (
);

  mux8 mux8_1 ();  // open: in_1, in_2, in_3, in_4, in_5, in_6, in_7, in_8, in_9, in_10, in_11, out_12
endmodule

module half_adder (
  input  in_1,
  input  in_2,
  output out_3,
  output out_4
);

  xor xor_1 (out_3, in_1, in_2);
  and and_1 (out_4, in_1, in_2);
endmodule

module full_adder_2bits (
  input  A,
  input  B,
  input  Ci,
  output R,
  output C
);

  wire and_1_out, and_2_out, and_3_out, xor_1_out;

  xor xor_1 (xor_1_out, A, B);
  and and_1 (and_1_out, A, B);
  and and_2 (and_2_out, A, Ci);
  and and_3 (and_3_out, Ci, B);
  xor xor_2 (R, xor_1_out, Ci);
  or or_1 (C, and_1_out, and_2_out, and_3_out);
endmodule

module full_adder_8bits (
  input  in_1,
  input  [7:0] B,
  input  [7:0] A,
  output [7:0] R,
  output out_5
);

  wire full_adder_2bits_1_c, full_adder_2bits_2_c, full_adder_2bits_3_c, full_adder_2bits_4_c,
       full_adder_2bits_5_c, full_adder_2bits_6_c, full_adder_2bits_7_c;

  full_adder_2bits full_adder_2bits_1 (.A(A[0]), .B(B[0]), .R(R[0]), .C(full_adder_2bits_1_c), .Ci(in_1));
  full_adder_2bits full_adder_2bits_2 (
    .A(A[1]), .B(B[1]), .R(R[1]), .C(full_adder_2bits_2_c), .Ci(full_adder_2bits_1_c));
  full_adder_2bits full_adder_2bits_3 (
    .A(A[2]), .B(B[2]), .R(R[2]), .C(full_adder_2bits_3_c), .Ci(full_adder_2bits_2_c));
  full_adder_2bits full_adder_2bits_4 (
    .A(A[3]), .B(B[3]), .R(R[3]), .C(full_adder_2bits_4_c), .Ci(full_adder_2bits_3_c));
  full_adder_2bits full_adder_2bits_5 (
    .A(A[4]), .B(B[4]), .R(R[4]), .C(full_adder_2bits_5_c), .Ci(full_adder_2bits_4_c));
  full_adder_2bits full_adder_2bits_6 (
    .A(A[5]), .B(B[5]), .R(R[5]), .C(full_adder_2bits_6_c), .Ci(full_adder_2bits_5_c));
  full_adder_2bits full_adder_2bits_7 (
    .A(A[6]), .B(B[6]), .R(R[6]), .C(full_adder_2bits_7_c), .Ci(full_adder_2bits_6_c));
  full_adder_2bits full_adder_2bits_8 (.A(A[7]), .B(B[7]), .R(R[7]), .C(out_5), .Ci(full_adder_2bits_7_c));
endmodule
